// Logisim project Vira.circ as structural Verilog: 1 circuit, main circuit main
module main (
);

  wire Clock_out;
  wire [31:0] adder_1_out, Current_Num_q, Hex_Ouput_q, Previous_Num_q;

  Clock Clock (.out(Clock_out));
  Register #(.width(32)) Current_Num (.D(adder_1_out), .Q(Current_Num_q), .clk(Clock_out));  // open: en, clr
  Register #(.width(32)) Previous_Num (.D(Current_Num_q), .Q(Previous_Num_q), .clk(Clock_out));  // open: en, clr
  Adder #(.width(32)) adder_1 (.a(Current_Num_q), .b(Previous_Num_q), .out(adder_1_out));  // open: cin, cout
  Register #(.width(32)) Hex_Ouput (.D(adder_1_out), .Q(Hex_Ouput_q), .clk(Clock_out));  // open: en, clr
  // Probe on Hex_Ouput_q

  // Notes on the sheet:
  //   19BEC100_19BEC108_Virahanka Number Generator
  //   Adder
  //   Virahanka_Num
endmodule
